# Fritzing sketch Schematic (saved by Fritzing 0.8.7b)
breadboards: 1

parts:
  Part1 = Pro Trinket 3.3V
  OLED1 = 128x64 Monochrom OLED Display with SPI Control
  RTC1 = DS1307 RTC Breakout

nets:
  GND: Part1.GND, RTC1.GND
  +3V3: Part1.+3V3, RTC1.5V
  N1: Part1.D4, OLED1.Reset
  N2: Part1.A4, OLED1.Data, RTC1.SDA
  N3: Part1.A5, OLED1.Clock, RTC1.SCL

custom parts:
  Pro Trinket 3.3V: The Pro Trinket 3.3V is like an Arduino Pro Mini with more pins and USB included. However, it uses 3V logic and 12MHz clock which means it's good when you want a lower-power and lower-voltage setup. Built with the common core Arduino chip, the ATmega328p, it has 18 GPIO, 2 extra analog inputs, 28K of flash, and 2K of RAM. It has onboard USB bootloading support with Optiboot support, so you can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
  DS1307 RTC Breakout: DS1307 Real-time Clock Breakout Board with Battery
